# Fritzing sketch RXB8_Raspi (saved by Fritzing 0.9.3b)

parts:
  U1 = RXB8 [package=rf-link_rx]
  R2 = Resistor [tolerance=±5% resistance=2.2k package="0805 [SMD]"]
  R1 = Resistor [tolerance=±5% resistance=1k package="0805 [SMD]"]
  Raspberry_Pi_1 = Raspberry Pi 3 [part_number=RPI-3-V1.2]

nets:
  N1: U1.DATA, R1.Pin_0
  +5V: U1.+5V, Raspberry_Pi_1.5V
  antenna: U1.ANT
  GND: U1.GND, R2.Pin_1, Raspberry_Pi_1.GND
  N2: R2.Pin_0, R1.Pin_1, Raspberry_Pi_1.GPIO17

notes:
  2k2
  1k

custom parts:
  RXB8: RXB8 Super Heterodyne Receiver Module
